# Fritzing sketch Schematic (saved by Fritzing 0.9.3b)
breadboards: 1

parts:
  Part1 = Arduino Mega ADK (Rev3)
  Q1 = Basic FET N-Channel [package="D2Pak [SMD]"]
  D1 = Rectifier Diode [part_number=1N4001 package="300 mil [THT]"]
  L1 = Solenoid
  RE1 = Rotary Encoder [package=THT]
  R1 = Resistor [tolerance=±5% resistance=220 package=THT]
  Part2 = 12 NeoPixel Ring [part_number=1643]
  NEOPIXEL1 = Neopixel Strip -- White (60/m)
  VCC1 = Battery
  Part3 = Arduino Mega ADK (Rev3)
  VCC2 = Battery  # not connected

nets:
  GND: Part1.GND, Q1.source, RE1.EncoderPinA, Part2.GND, NEOPIXEL1.GND, VCC1.-, Part3.GND
  N1: Part1.5V, RE1.EncoderPinB
  N2: Part1.VIN, D1.cathode, L1.pin2
  N3: Part1.D2_PWM, RE1.EncoderPinC
  N4: Part1.D4_PWM, R1.Pin_1
  N5: Part1.D7_PWM, NEOPIXEL1.+5V
  N6: Q1.Gate, R1.Pin_0
  N7: Q1.drain, D1.anode, L1.pin1
  N8: Part2.IN, Part3.D7_PWM
  N9: Part2.VDD, NEOPIXEL1.DI, VCC1.+

notes:
  Valve
  Liquid flow meter
  5v 10
  Power Supply Unit
  Arduino A
  (Valve, Flow meter
  & Payment Strip)
  Arduino B
  (Beer Mat Strip)
  12V 1.2A
  Power Suppl y Unit

custom parts:
  12 NeoPixel Ring: 12 ultra bright smart LED NeoPixels are arranged in a circle with 1.5" (37mm) outer diameter. The rings are 'chainable' - connect the output pin of one to the input pin of another. Use only one microcontroller pin to control as many as you can chain together! Each LED is addressable as the driver chip is inside the LED. Each one has ~18mA constant current drive so the color will be very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
  Neopixel Strip -- White (60/m): Neopixel Strip, White, 60 pixels per meter.
